# Fritzing sketch voice_controlled_robot (saved by Fritzing 0.9.3b)
breadboards: 1

parts:
  Part1 = Arduino Uno (Rev3) - ICSP
  S1 = H-Bridge with L298N
  Part2 = Bluetooth HC-05 Macho
  M1 = DC Motor
  M3 = DC Motor
  M4 = DC Motor
  BAT1 = BC9VPC [package=bc9vpc]
  M5 = DC Motor

nets:
  N1: Part1.D9_PWM, S1.IN4
  N2: Part1.D10_PWM/SS, Part2.TXD
  N3: Part1.D11_PWM/MOSI, Part2.RXD
  GND: Part1.GND, S1.GND, Part2.GND, BAT1.V-
  N4: Part1.D3_PWM, S1.IN1
  N5: Part1.D5_PWM, S1.IN2
  N6: Part1.D6_PWM, S1.IN3
  VIN: Part1.VIN, S1.12V, Part2.VCC, BAT1.V+
  N7: S1.OUT3-Motor2, M1.pin_2, M3.pin_2
  N8: S1.OUT4-Motor2, M1.pin_1, M3.pin_1
  N9: S1.OUT1-Motor1, M4.pin_2, M5.pin_2
  N10: S1.OUT2-Motor1, M4.pin_1, M5.pin_1

custom parts:
  H-Bridge with L298N: h-bridge
